// Digital circuit alu-32b-final.dig as structural Verilog
module alu_32b_final (
  input  [31:0] A,
  input  nz0,
  input  [31:0] B,
  input  [7:0] Opcode,
  input  [4:0] control,
  input  [31:0] REG_C,
  input  cin_sel,
  input  FLAG_C,
  output vout,
  output zout,
  output nzout,
  output nout,
  output [31:0] Out,
  output cout
);

  wire c7, c15, c23, nz1, nz2, nz3;
  wire [7:0] c0_7, c8_15, c16_23, c24_31;
  wire [31:0] multiplexer_1_out;

  Multiplexer #(.Bits(32)) multiplexer_1 (
    .sel(cin_sel), .in_0({{31{1'b0}}, FLAG_C}), .in_1(32'h1), .out(multiplexer_1_out));
  Multiplexer #(.Bits(32)) multiplexer_2 (
    .sel(control[4]), .in_0(multiplexer_1_out), .in_1(REG_C), .out({c24_31, c16_23, c8_15, c0_7}));
  not not_1 (zout, nzout);
  alu_8b_final Cell_0 (
    .opcode(Opcode), .control(control), .A(A[7:0]), .B(B[7:0]), .C(c0_7), .nz_in(nz0), .cin(c0_7[0]),
    .out(Out[7:0]), .nz_out(nz1), .cout(c7));  // open: vout, zout, n
  alu_8b_final Cell_1 (
    .opcode(Opcode), .control(control), .A(A[15:8]), .B(B[15:8]), .C(c8_15), .nz_in(nz2), .cin(c7),
    .out(Out[15:8]), .nz_out(nz3), .cout(c15));  // open: vout, zout, n
  alu_8b_final Cell_2 (
    .opcode(Opcode), .control(control), .A(A[23:16]), .B(B[23:16]), .C(c16_23), .nz_in(nz1), .cin(c15),
    .out(Out[23:16]), .nz_out(nz2), .cout(c23));  // open: vout, zout, n
  alu_8b_final Cell_3 (
    .opcode(Opcode), .control(control), .A(A[31:24]), .B(B[31:24]), .C(c24_31), .nz_in(nz3), .cin(c23),
    .out(Out[31:24]), .vout(vout), .nz_out(nzout), .n(nout), .cout(cout));  // open: zout

  // Other names for the same wires on the sheet: a0_7[7:0] = A[7:0]; a8_15[7:0] = A[15:8]; a16_23[7:0] = A[23:16];
  //   a24_31[7:0] = A[31:24]; b0_7[7:0] = B[7:0]; b8_15[7:0] = B[15:8]; b16_23[7:0] = B[23:16];
  //   b24_31[7:0] = B[31:24]; ceff[31:0] = {c24_31, c16_23, c8_15, c0_7}; cin0 = c0_7[0]; asel = control[0];
  //   ainv = control[1]; bsel = control[2]; binv = control[3]; csel = control[4]; FLAG_C32[0] = FLAG_C;
  //   out0_7[7:0] = Out[7:0]; out8_15[7:0] = Out[15:8]; out16_23[7:0] = Out[23:16]; out24_31[7:0] = Out[31:24]

  // Notes on the sheet:
  //   A: default 9
  //   B: default 20
  //   Opcode: default 150
  //   control: default 21
endmodule

/* Test case:
A nz0 B REG_C Opcode control cin-sel FLAG_C Out vout zout nzout nout cout

# SECTION 1: CPU microcode encodings (main.v ALU paths)
# ADD — microcode 0x01
0x00000005 0 0x00000003 0x00000000 0x96 5 0 0 0x00000008 0 0 1 0 0
0xFFFFFFFF 0 0x00000001 0x00000000 0x96 5 0 0 0x00000000 0 1 0 0 1
0x80000000 0 0x80000000 0x00000000 0x96 5 0 0 0x00000000 1 1 0 0 1

# SUB — microcode 0x02
0x0000000A 0 0x00000003 0x00000000 0x96 13 1 0 0x00000007 0 0 1 0 1
0x00000005 0 0x0000000A 0x00000000 0x96 13 1 0 0xFFFFFFFB 0 0 1 1 0

# AND — microcode 0x03
0xFF00FF00 0 0x0F0F0F0F 0x00000000 0x88 5 0 0 0x0E0F0E00 0 0 1 0 1

# OR — microcode 0x04
0xFF00FF00 0 0x0F0F0F0F 0x00000000 0xEE 5 0 0 0xFF1FFF0F 0 0 1 1 1

# XOR — microcode 0x05
0xFF00FF00 0 0x0F0F0F0F 0x00000000 0x66 5 0 0 0xF110F10F 0 0 1 1 1

# NOT — microcode 0x06
0xAAAAAAAA 0 0x00000000 0x00000000 0x33 1 0 0 0xFFFFFFFF 0 0 1 1 0

# LDI_pass_B — microcode 0x22 literal on B
0x00000000 0 0x0000DEAD 0x00000000 0xCC 4 0 0 0x0000DEAD 0 0 1 0 0
0x00000000 0 0x12345678 0x00000000 0xCC 4 0 0 0x12345678 0 0 1 0 0

# LUT3_PASS_C — LUT3 addr-csel=1
0xFFFFFFFF 0 0x00000000 0x55555555 0xAA 21 0 0 0x55555555 0 0 1 0 1

# LUT2_XOR — direct LUT2 band
0xF0F0F0F0 0 0x0F0F0F0F 0x00000000 0x3C 5 0 0 0xFFFFFFFF 0 0 1 1 0

# SECTION 2: carry / overflow corner cases (ADD)
0x7FFFFFFF 0 0x00000001 0x00000000 0x96 5 0 0 0x80000000 1 0 1 1 0
0x80000000 0 0xFFFFFFFF 0x00000000 0x96 5 0 0 0x7FFFFFFF 1 0 1 0 1
0x0000000A 0 0x00000005 0x00000000 0x96 5 0 0 0x0000000F 0 0 1 0 0

# SECTION 3: 3-input LUT samples (control=10101)
0xAAAAAAAA 0 0x00000000 0x55555555 0x5A 21 0 0 0xFFFFFFFF 0 0 1 1 0
0xAAAAAAAA 0 0x00000000 0x55555555 0xA0 21 0 0 0x00000000 0 1 0 0 0
0xAAAAAAAA 0 0x00000000 0x55555555 0xFA 21 0 0 0xFFFFFFFF 0 0 1 1 0
*/
