// Digital circuit main.dig as structural Verilog
module main (
  input  clk,
  input  reset,
  output [23:0] pc_out,
  output [31:0] mem_din,
  output [31:0] ir_bus,
  output [23:0] ir_offset,
  output [23:0] ir_addr,
  output [7:0] ir_addr_w,
  output [7:0] ir_addr_b,
  output [2:0] wb_sel,
  output [7:0] ir_opcode,
  output [7:0] ctrl_alu_op,
  output [31:0] alu_out,
  output [31:0] reg_w_data,
  output [31:0] p,
  output [15:0] term_data,
  output [15:0] vram_addr,
  output term_we,
  output [23:0] pc_save,
  output [31:0] m_out,
  output [23:0] mem_addr,
  output [2:0] ctrl_w_sel,
  output [31:0] reg_b,
  output [31:0] reg_a,
  output ctrl_reg_we,
  output [7:0] ir_addr_a,
  output [3:0] ir_sel
);

  wire alu_cout, alu_nout, alu_nzout, alu_vout, alu_zout, and_3_out, and_4_out, comparator_1_eq,
       comparator_2_eq, ctrl_addr_csel, ctrl_branch_en, ctrl_cin_sel, ctrl_cycles, ctrl_flags_we,
       ctrl_jump_type, ctrl_mem_rd, ctrl_mem_wr, ctrl_shift_op, flag_c, flag_n, flag_v, flag_z, HALT_IN,
       is_mmio, mem_rd_out, mem_sel, pc_branch_en, pc_jump_uncond, pc_mux_sel_1, pc_mux_sel_2, ram_cs,
       seq_exec, seq_fetch, sp_load_n, vram_we;
  wire [1:0] c_addr_msb2, ctrl_sp_op;
  wire [2:0] cond, ctrl_bus_sel;
  wire [4:0] ctrl_alu_pre;
  wire [15:0] vram_data;
  wire [23:0] CPU_ADDR_OUT, mem_addr_in, mmio_addr, sp_delta, sp_out;
  wire [31:0] io_data_in, mul_out, reg_c, shift_out;

  and and_1 (pc_branch_en, ctrl_branch_en, seq_exec);
  and and_2 (pc_jump_uncond, ctrl_jump_type, seq_exec);
  // sequencer sequencer_1: pin names not known; wires that end beside it: reset, ctrl_cycles, clk, seq_fetch, seq_exec
  pc pc_1 (
    .CLK(clk), .nSR(reset), .ADDR_ABS(ir_addr), .OFFSET(ir_offset), .ADDR_RET(pc_save),
    .MUX1_SEL(pc_mux_sel_1), .MUX2_SEL(pc_mux_sel_2), .FLAG_N(flag_n), .FLAG_C(flag_c), .FLAG_Z(flag_z),
    .FLAG_O(flag_v), .COND(cond), .BRANCH_EN(pc_branch_en), .INT_EN_IN(1'b0), .HALT_IN(HALT_IN),
    .INT_REQ(1'b0), .INT_VEC_0(1'b1), .INT_VEC_1(1'b1), .INT_VEC_2(1'b1), .SP_DELTA(sp_delta),
    .SP_LOAD_N(sp_load_n), .JUMP_UNCOND(pc_jump_uncond), .PCEN(seq_fetch), .PC_OUT(pc_out), .SP_OUT(sp_out),
    .PC_SAVE(pc_save));  // open: INT_EN, HALTED, INT_ACK, FLAGS_SAVE
  register register_1 (
    .WE(ctrl_reg_we), .DATA_W(reg_w_data), .ADDR_A(ir_addr_a), .ADDR_B(ir_addr_b), .ADDR_W(ir_addr_w),
    .EXEC(seq_exec), .addr_c_sel(ctrl_addr_csel), .ir_bus(ir_bus), .clk(clk), .DATA_A(reg_a), .DATA_B(reg_b),
    .DATA_C(reg_c));
  ir ir_1 (
    .DATA_IN(mem_din), .LOAD(seq_fetch), .CLK(clk), .ir_sel(ir_sel), .RegB(reg_b), .OPCODE(ir_opcode),
    .ADDR_A(ir_addr_a), .ADDR_B(ir_addr_b), .ADDR_W(ir_addr_w), .ADDR_ABS(ir_addr), .OFFSET(ir_offset),
    .COND(cond), .ir_imm_out(ir_bus));  // open: MUX1_SEL, MUX2_SEL
  bus_arbitration bus_arbitration_1 (
    .FETCH(seq_fetch), .IR_ADDR(ir_addr), .MEM_RD_IN(ctrl_mem_rd), .addr_sel(ctrl_bus_sel), .Reg_b(reg_b),
    .Pc_out(pc_out), .SP_out(sp_out), .Alu_in(alu_out), .ADDR_BUS(mem_addr), .MEM_RD_OUT(mem_rd_out));
  io_controller io_controller_1 (
    .mem_addr(mmio_addr), .c_wr(ctrl_mem_wr), .kb_data(16'h1), .mem_data_out(reg_b), .io_data_in(io_data_in),
    .ram_cs(ram_cs), .vram_we(vram_we), .vram_addr(vram_addr), .vram_data(vram_data), .term_we(term_we),
    .term_data(term_data));
  EEPROMDualPort #(.AddrBits(24), .Bits(32)) eepromdualport_1 (
    .A(CPU_ADDR_OUT), .Din(reg_b), .str(ctrl_mem_wr), .C(clk), .ld(mem_rd_out), .D(m_out));
  // microcode microcode_1: pin names not known; wires that end beside it: ir_opcode, ctrl_alu_op, ctrl_alu_pre, ctrl_cin_sel, ctrl_shift_op, ir_sel, ctrl_addr_csel, ctrl_w_sel, ctrl_reg_we, ctrl_flags_we, ctrl_mem_rd, ctrl_mem_wr, mem_sel, ctrl_branch_en, ctrl_jump_type, ctrl_sp_op, pc_mux_sel_1, ctrl_cycles, ctrl_bus_sel
  mmio_bus mmio_bus_1 (
    .ADDR(mem_addr), .CPU_ADDR_OUT(CPU_ADDR_OUT), .mmio_addr(mmio_addr), .is_mmio(is_mmio),
    .cpu_addr_msb2(c_addr_msb2));
  Comparator #(.Bits(8)) comparator_1 (.a(8'h2), .b(ir_addr_w), .eq(comparator_1_eq));  // open: gt, lt
  mul_div mul_div_1 (.A(reg_a), .B(ir_bus), .mul_out(mul_out));
  // byte_lane_decoder byte_lane_decoder_1: pin names not known; wires that end beside it: m_out, mem_sel, io_data_in, c_addr_msb2, mem_din
  and and_3 (and_3_out, seq_exec, ctrl_reg_we, comparator_1_eq);
  // shift shift_1: pin names not known; wires that end beside it: reg_a, ctrl_shift_op, ir_bus, shift_out
  alu_32b_final alu_32b_final_1 (
    .A(reg_a), .nz0(1'b0), .B(ir_bus), .Opcode(ctrl_alu_op), .control(ctrl_alu_pre), .REG_C(reg_c),
    .cin_sel(ctrl_cin_sel), .FLAG_C(flag_c), .vout(alu_vout), .zout(alu_zout), .nzout(alu_nzout),
    .nout(alu_nout), .Out(alu_out), .cout(alu_cout));
  flag_reg flag_reg_1 (
    .ZERO_IN(alu_zout), .CARRY_IN(alu_cout), .NEGATIVE_IN(alu_nout), .OVERFLOW_IN(alu_vout),
    .FLAG_WE(ctrl_flags_we), .CLK(clk), .EXEC(seq_exec), .FLAG_Z(flag_z), .FLAG_C(flag_c), .FLAG_N(flag_n),
    .FLAG_O(flag_v));
  wb_mux wb_mux_1 (
    .wb_sel(ctrl_w_sel), .alu_out(alu_out), .shift_out(shift_out), .pc_save(pc_save), .mem_din(io_data_in),
    .io_datain(reg_a), .reg_a(ir_bus), .ir_bus(mul_out), .reg_w_data(reg_w_data));
  Register #(.Bits(32)) register_2 (.D(ir_bus), .C(clk), .en(and_3_out), .Q(p));
  Multiplexer #(.Bits(24)) multiplexer_1 (.sel(and_4_out), .in_0(CPU_ADDR_OUT), .in_1(mmio_addr), .out(mem_addr_in));
  and and_4 (and_4_out, is_mmio, mem_rd_out);
  and and_5 (HALT_IN, comparator_2_eq, seq_exec);
  Comparator #(.Bits(8)) comparator_2 (.a({8{1'b1}}), .b(ir_opcode), .eq(comparator_2_eq));  // open: gt, lt
  Comparator #(.Bits(8)) comparator_3 (.a(ir_bus[31:24]), .b(8'h33), .eq(pc_mux_sel_2));  // open: gt, lt
  Multiplexer #(.Selector_Bits(2), .Bits(24)) multiplexer_2 (
    .sel(ctrl_sp_op), .in_0({24{1'b0}}), .in_1(24'h1), .in_2({24{1'b1}}), .in_3({24{1'b0}}), .out(sp_delta));
  nor nor_1 (sp_load_n, ctrl_sp_op[0], ctrl_sp_op[1]);

  assign wb_sel = ctrl_w_sel;

  // Other names for the same wires on the sheet: ctrl_wb_sel[2:0] = ctrl_w_sel; ir_24_31[7:0] = ir_bus[31:24];
  //   mem_ram_out[31:0] = m_out

  // Notes on the sheet:
  //   reset: default 1
  //   contents of eepromdualport_1 (hex, n*v repeats v):
  //   10000000,1000A001,1000A002,01020102,62000003
endmodule

/* Test case add-arithmetic-only:
reset clk alu-out ctrl-reg-we ir-opcode ctrl-alu-op wb-sel reg-a reg-b reg-w-data ir-addr-a ir-addr-b ir-addr-w pc-out
# EEPROM[0]=0x01010203 ADD r3,r1,r2 (r1=r2=0)
1 0 x x x x x x x x x x x x
1 1 x x x x x x x x x x x x
1 0 x x x x x x x x x x x x
# EXECUTE ADD: r1+r2=0, operands read from reg file, wb from ALU
1 1 0 1 0x01 0x96 0 0 0 0 1 2 3 1
*/

/* Test case load-store-chain:
reset clk alu-out ctrl-reg-we ir-opcode ctrl-alu-op wb-sel mem-addr reg-w-data
# ADD(inst[0]) -> LW(inst[1]) -> SW(inst[2]) — arithmetic at each EXECUTE
1 0 x x x x x x x
1 1 x x x x x x x
1 0 x x x x x x x
# EXECUTE ADD: 0+0=0
1 1 0 1 0x01 0x96 0 x 0
1 0 x x x x x x x
1 1 x x x x x x x
1 0 x x x x x x x
1 1 x x x x x x x
1 0 x x x x x x x
# EXECUTE LW: r0+4=4, wb=mem
1 1 4 1 0x30 0x96 3 4 0xCAFEBABE
1 0 x x x x x x x
1 1 x x x x x x x
1 0 x x x x x x x
1 1 x x x x x x x
1 0 x x x x x x x
# EXECUTE SW: r0+5=5, no reg write
1 1 5 0 0x40 0x96 x 5 x
*/

/* Test case lw-pipeline:
reset clk alu-out mem-din ctrl-reg-we ir-opcode ir-addr-w ctrl-alu-op wb-sel mem-addr reg-w-data
# EEPROM[0]=ADD, [1]=LW r80,[r0+4] (30004050), mem[4]=0xCAFEBABE
1 0 x x x x x x x x x
1 1 x x x x x x x x x
1 0 x x x x x x x x x
# EXECUTE ADD: r1+r2=0
1 1 0 x 1 0x01 3 0x96 0 x 0
1 0 x x x x x x x x x
1 1 x x x x x x x x x
1 0 x x x x x x x x x
1 1 x x x x x x x x x
1 0 x x x x x x x x x
# EXECUTE LW: address ALU r0+4=4, load mem[4]
1 1 4 0xCAFEBABE 1 0x30 0x50 0x96 3 4 0xCAFEBABE
*/
